// Logisim project Cache.circ as structural Verilog: 9 circuits, main circuit implementation
module implementation (
  input  [9:0] CpuAddressIn,
  input  CpuReadIn,
  input  CpuWriteIn,
  input  [7:0] CpuWriteValueIn,
  input  [31:0] LineFromMemIn,
  input  ClkIn,
  output ReadyOut,
  output DidContainOut,
  output [7:0] ByteReadOut,
  output [7:0] MemAddressOut,
  output MemReadOut,
  output MemWriteOut,
  output [31:0] Line2MemOut
);

  wire InitializeCtr, IsDirty_Ctr, IsValidValue, multiplexer_3_out, multiplexer_4_out, oldestWayIsDirty,
       savedCpuRead, savedCpuWrite, set0Contain, set0OldestWayIsDrity, set1Contain, set1OldestWayIsDrity,
       setBit, UpdateAgeCtr, UpdateConentCtr;
  wire [1:0] offsetBit;
  wire [2:0] fsmnextstate_1_nextstate, register_2_q;
  wire [6:0] oldestWayTagBits, set0OldestWayTag, set1OldestWayTag, tagBit;
  wire [7:0] savedCpuWriteValue, set0ByteRead, set1ByteRead;
  wire [31:0] oldestWayContent, set0OldestWayContent, set1OldestWayContent;

  Register register_1 (.D(CpuWriteValueIn), .en(ReadyOut), .clk(ClkIn), .Q(savedCpuWriteValue));  // open: clr
  Multiplexer #(.enable("false"), .width(32)) multiplexer_1 (
    .in1(oldestWayContent), .out(Line2MemOut), .sel(MemWriteOut));  // open: in0
  FsmNextState fsmnextstate_1 (
    .didContain_In(DidContainOut), .IsDirty_In(oldestWayIsDirty), .CpuRead_In(savedCpuRead),
    .CpuWrite_In(savedCpuWrite), .CurrentState(register_2_q), .NextState(fsmnextstate_1_nextstate));
  Multiplexer #(.enable("false"), .width(8)) multiplexer_2 (
    .in0({tagBit, setBit}), .in1({oldestWayTagBits, setBit}), .out(MemAddressOut), .sel(MemWriteOut));
  Register #(.width(3)) register_2 (
    .D(fsmnextstate_1_nextstate), .en(1'b1), .clk(ClkIn), .Q(register_2_q));  // open: clr
  Register #(.width(10)) savedCpuAddress (
    .D(CpuAddressIn), .en(ReadyOut), .clk(ClkIn), .Q({tagBit, setBit, offsetBit}));  // open: clr
  Register #(.width(1)) register_3 (.D(CpuReadIn), .en(ReadyOut), .clk(ClkIn), .Q(savedCpuRead));  // open: clr
  Register #(.width(1)) register_4 (.D(CpuWriteIn), .en(ReadyOut), .clk(ClkIn), .Q(savedCpuWrite));  // open: clr
  // Probe on offsetBit
  // Probe on tagBit
  // Probe on setBit
  OutputCircuit outputcircuit_1 (
    .CurrentState(register_2_q), .Ready_Ctr(ReadyOut), .MemRead_Ctr(MemReadOut), .MemWrite_Ctr(MemWriteOut),
    .Initialize_Ctr(InitializeCtr), .UpdateAge_Ctr(UpdateAgeCtr), .IsValid_Value(IsValidValue),
    .IsDirty_Ctr(IsDirty_Ctr), .UpdateContent_Ctr(UpdateConentCtr));
  Multiplexer #(.enable("false")) multiplexer_3 (.in0(1'b1), .in1(1'b0), .out(multiplexer_3_out), .sel(setBit));
  Multiplexer #(.enable("false")) multiplexer_4 (.in0(1'b0), .in1(1'b1), .out(multiplexer_4_out), .sel(setBit));
  Set set0 (
    .tagIn(tagBit), .offsetIn(offsetBit), .enable(multiplexer_3_out), .read(savedCpuRead),
    .write(savedCpuWrite), .writeValue(savedCpuWriteValue), .clock(ClkIn),
    .UpdateContentCtr(UpdateConentCtr), .contentIn(LineFromMemIn), .UpdateAgeCtr(UpdateAgeCtr),
    .IsValidValue(IsValidValue), .IsDirty_Ctr(IsDirty_Ctr), .InitializeCtr(InitializeCtr),
    .ReadBlock(MemReadOut), .isContainOut(set0Contain), .oldestWayIfDirty(set0OldestWayIsDrity),
    .oldestWayContent(set0OldestWayContent), .oldestWayTag(set0OldestWayTag), .ByteReadOut(set0ByteRead));
  Set set1 (
    .tagIn(tagBit), .offsetIn(offsetBit), .enable(multiplexer_4_out), .read(savedCpuRead),
    .write(savedCpuWrite), .writeValue(savedCpuWriteValue), .clock(ClkIn),
    .UpdateContentCtr(UpdateConentCtr), .contentIn(LineFromMemIn), .UpdateAgeCtr(UpdateAgeCtr),
    .IsValidValue(IsValidValue), .IsDirty_Ctr(IsDirty_Ctr), .InitializeCtr(InitializeCtr),
    .ReadBlock(MemReadOut), .isContainOut(set1Contain), .oldestWayIfDirty(set1OldestWayIsDrity),
    .oldestWayContent(set1OldestWayContent), .oldestWayTag(set1OldestWayTag), .ByteReadOut(set1ByteRead));
  // Probe on set1ByteRead
  // Probe on set0ByteRead
  Multiplexer #(.enable("false")) multiplexer_5 (
    .in0(set0Contain), .in1(set1Contain), .out(DidContainOut), .sel(setBit));
  Multiplexer #(.enable("false"), .width(8)) multiplexer_6 (
    .in0(set0ByteRead), .in1(set1ByteRead), .out(ByteReadOut), .sel(setBit));
  Multiplexer #(.enable("false")) multiplexer_7 (
    .in0(set0OldestWayIsDrity), .in1(set1OldestWayIsDrity), .out(oldestWayIsDirty), .sel(setBit));
  Multiplexer #(.enable("false"), .width(7)) multiplexer_8 (
    .in0(set0OldestWayTag), .in1(set1OldestWayTag), .out(oldestWayTagBits), .sel(setBit));
  Multiplexer #(.enable("false"), .width(32)) multiplexer_9 (
    .in0(set0OldestWayContent), .in1(set1OldestWayContent), .out(oldestWayContent), .sel(setBit));

  // Other names for the same wires on the sheet: clk = ClkIn; CpuAddress[9:0] = CpuAddressIn; CpuRead = CpuReadIn;
  //   CpuWrite = CpuWriteIn; CpuWriteValue[7:0] = CpuWriteValueIn; DidContain = DidContainOut;
  //   MemAddress[7:0] = MemAddressOut; MemRead = MemReadOut; MemReadCtr = MemReadOut; MemWrite = MemWriteOut;
  //   MemWriteCtr = MemWriteOut; Ready = ReadyOut; ReadyCtr = ReadyOut; LineFromMem[31:0] = LineFromMemIn;
  //   savedLineFromMem[31:0] = LineFromMemIn; ByteRead[7:0] = ByteReadOut; SelectedSetByteRead[7:0] = ByteReadOut;
  //   Line2Mem[31:0] = Line2MemOut; SelectedSetLine2Mem[31:0] = Line2MemOut

  // Notes on the sheet:
  //   MemWrite -> Writeback:
endmodule

module Set (
  input  [6:0] tagIn,
  input  [1:0] offsetIn,
  input  enable,
  input  read,
  input  write,
  input  [7:0] writeValue,
  input  clock,
  input  UpdateContentCtr,
  input  [31:0] contentIn,
  input  UpdateAgeCtr,
  input  IsValidValue,
  input  IsDirty_Ctr,
  input  InitializeCtr,
  input  ReadBlock,
  output isContainOut,
  output oldestWayIfDirty,
  output [31:0] oldestWayContent,
  output [6:0] oldestWayTag,
  output [7:0] ByteReadOut
);

  wire and_1_out, and_2_out, and_3_out, and_4_out, and_5_out, and_6_out, and_7_out, and_8_out, and_9_out,
       and_10_out, and_11_out, and_12_out, comparator_7_eq, comparator_8_eq, comparator_9_eq, way0Contain,
       way0IsDirty, way0Valid, way1Contain, way1IsDirty, way1Valid, way2Contain, way2IsDirty, way2Valid;
  wire [0:0] and_13_out;
  wire [1:0] CurrentAge, matchingWay, oldestWay, way0Age, way0NextAge, way1Age, way1NextAge, way2Age,
       way2NextAge;
  wire [2:0] comparator_1_eq, comparator_4_eq;
  wire [6:0] way0tag, way1tag, way2tag;
  wire [7:0] multiplexer_2_out, multiplexer_3_out, multiplexer_4_out;
  wire [31:0] NewContent, way0Content, way1Content, way2Content, writenewcontent_1_out_7;

  Comparator #(.width(7)) comparator_1 (.a(tagIn), .b(way0tag), .eq(comparator_1_eq[0]));  // open: gt, lt
  Comparator #(.width(7)) comparator_2 (.a(tagIn), .b(way1tag), .eq(comparator_1_eq[1]));  // open: gt, lt
  Comparator #(.width(7)) comparator_3 (.a(tagIn), .b(way2tag), .eq(comparator_1_eq[2]));  // open: gt, lt
  Comparator #(.mode("unsigned"), .width(2)) comparator_4 (
    .a(way0Age), .b(2'b10), .eq(comparator_4_eq[0]));  // open: gt, lt
  Comparator #(.mode("unsigned"), .width(2)) comparator_5 (
    .a(way1Age), .b(2'b10), .eq(comparator_4_eq[1]));  // open: gt, lt
  Comparator #(.mode("unsigned"), .width(2)) comparator_6 (
    .a(way2Age), .b(2'b10), .eq(comparator_4_eq[2]));  // open: gt, lt
  BitFinder #(.width(3)) bitfinder_1 (.in(comparator_1_eq), .index(matchingWay));  // open: found
  BitFinder #(.width(3)) bitfinder_2 (.in(comparator_4_eq), .index(oldestWay));  // open: found
  NextAge nextage_1 (
    .way0Age(way0Age), .way1Age(way1Age), .way2Age(way2Age), .CurrentAge(CurrentAge),
    .way0NextAge(way0NextAge), .way1NextAge(way1NextAge), .way2NextAge(way2NextAge));
  FindCurrentAgeSimple findcurrentagesimple_1 (
    .Way0Age(way0Age), .Way1Age(way1Age), .Way2Age(way2Age), .matchingWay(matchingWay),
    .CurrentAge(CurrentAge));
  and and_1 (and_1_out, UpdateAgeCtr, enable);
  and and_2 (and_2_out, UpdateAgeCtr, enable);
  and and_3 (and_3_out, UpdateContentCtr, enable);
  and and_4 (and_4_out, IsValidValue, enable);
  and and_5 (and_5_out, UpdateAgeCtr, enable);
  and and_6 (and_6_out, UpdateAgeCtr, enable);
  and and_7 (and_7_out, UpdateContentCtr, enable);
  and and_8 (and_8_out, IsValidValue, enable);
  and and_9 (and_9_out, UpdateAgeCtr, enable);
  and and_10 (and_10_out, UpdateContentCtr, enable);
  and and_11 (and_11_out, IsValidValue, enable);
  and and_12 (and_12_out, UpdateAgeCtr, enable);
  Way way0 (
    .NextAge(way0NextAge), .UpdateAgeCtr(and_2_out), .clock(clock), .UpdateContentCtr(and_3_out),
    .Tagin(tagIn), .newContent(NewContent), .IsValidValue(and_4_out), .IsDirty_Ctr(and_5_out),
    .WayIndex(2'b00), .InitializeCtr(InitializeCtr), .isValid(way0Valid), .ageOut(way0Age),
    .isDirty(way0IsDirty), .contentOut(way0Content), .tagOut(way0tag));
  Way way1 (
    .NextAge(way1NextAge), .UpdateAgeCtr(and_6_out), .clock(clock), .UpdateContentCtr(and_7_out),
    .Tagin(tagIn), .newContent(NewContent), .IsValidValue(and_8_out), .IsDirty_Ctr(and_9_out),
    .WayIndex(2'b01), .InitializeCtr(InitializeCtr), .isValid(way1Valid), .ageOut(way1Age),
    .isDirty(way1IsDirty), .contentOut(way1Content), .tagOut(way1tag));
  Way way2 (
    .NextAge(way2NextAge), .UpdateAgeCtr(and_1_out), .clock(clock), .UpdateContentCtr(and_10_out),
    .Tagin(tagIn), .newContent(NewContent), .IsValidValue(and_11_out), .IsDirty_Ctr(and_12_out),
    .WayIndex(2'b10), .InitializeCtr(InitializeCtr), .isValid(way2Valid), .ageOut(way2Age),
    .isDirty(way2IsDirty), .contentOut(way2Content), .tagOut(way2tag));
  and and_13 (and_13_out[0], write, UpdateContentCtr);
  WriteNewContent writenewcontent_1 (
    .Way0Content(way0Content), .Way1Content(way1Content), .Way2Content(way2Content), .Offset(offsetIn),
    .WriteValue(writeValue), .Matchingway(matchingWay), .out_7(writenewcontent_1_out_7));
  Multiplexer #(.enable("false"), .select(2), .width(32)) multiplexer_1 (
    .in1(writenewcontent_1_out_7), .in2(contentIn), .out(NewContent), .sel({ReadBlock, and_13_out[0]}));  // open: in0, in3
  Comparator #(.width(7)) comparator_7 (.a(way0tag), .b(tagIn), .eq(comparator_7_eq));  // open: gt, lt
  Comparator #(.width(7)) comparator_8 (.a(way1tag), .b(tagIn), .eq(comparator_8_eq));  // open: gt, lt
  Comparator #(.width(7)) comparator_9 (.a(way2tag), .b(tagIn), .eq(comparator_9_eq));  // open: gt, lt
  and and_14 (way0Contain, way0Valid, comparator_7_eq);
  and and_15 (way1Contain, way1Valid, comparator_8_eq);
  and and_16 (way2Contain, way2Valid, comparator_9_eq);
  or or_1 (isContainOut, way0Contain, way1Contain, way2Contain);
  Multiplexer #(.enable("false"), .select(2), .width(8)) multiplexer_2 (
    .in0(way0Content[7:0]), .in1(way0Content[15:8]), .in2(way0Content[23:16]), .in3(way0Content[31:24]),
    .out(multiplexer_2_out), .sel(offsetIn));
  Multiplexer #(.enable("false"), .select(2), .width(8)) multiplexer_3 (
    .in0(way1Content[7:0]), .in1(way1Content[15:8]), .in2(way1Content[23:16]), .in3(way1Content[31:24]),
    .out(multiplexer_3_out), .sel(offsetIn));
  Multiplexer #(.enable("false"), .select(2), .width(8)) multiplexer_4 (
    .in0(way2Content[7:0]), .in1(way2Content[15:8]), .in2(way2Content[23:16]), .in3(way2Content[31:24]),
    .out(multiplexer_4_out), .sel(offsetIn));
  Multiplexer #(.enable("false"), .select(2)) multiplexer_5 (
    .in0(way0IsDirty), .in1(way1IsDirty), .in2(way2IsDirty), .out(oldestWayIfDirty), .sel(oldestWay));  // open: in3
  Multiplexer #(.enable("false"), .select(2), .width(32)) multiplexer_6 (
    .in0(way0Content), .in1(way1Content), .in2(way2Content), .out(oldestWayContent), .sel(oldestWay));  // open: in3
  Multiplexer #(.enable("false"), .select(2), .width(7)) multiplexer_7 (
    .in0(way0tag), .in1(way1tag), .in2(way2tag), .out(oldestWayTag), .sel(oldestWay));  // open: in3
  Multiplexer #(.enable("false"), .select(2), .width(8)) multiplexer_8 (
    .in0(multiplexer_2_out), .in1(multiplexer_3_out), .in2(multiplexer_4_out), .out(ByteReadOut),
    .sel(matchingWay));  // open: in3

  // Other names for the same wires on the sheet: contain = isContainOut; offset[1:0] = offsetIn; tag[6:0] = tagIn;
  //   UpdateConentCtr = UpdateContentCtr

  // Notes on the sheet:
  //   Write Value or Read Block
  //   If cpuRead do this after update age
endmodule

module Way (
  input  [1:0] NextAge,
  input  UpdateAgeCtr,
  input  clock,
  input  UpdateContentCtr,
  input  [6:0] Tagin,
  input  [31:0] newContent,
  input  IsValidValue,
  input  IsDirty_Ctr,
  input  [1:0] WayIndex,
  input  InitializeCtr,
  output isValid,
  output [1:0] ageOut,
  output isDirty,
  output [31:0] contentOut,
  output [6:0] tagOut
);

  wire not_1_out;
  wire [1:0] multiplexer_1_out;

  Register Byte0 (.D(newContent[7:0]), .en(UpdateContentCtr), .clk(clock), .Q(contentOut[7:0]));  // open: clr
  Register Byte1 (.D(newContent[15:8]), .en(UpdateContentCtr), .clk(clock), .Q(contentOut[15:8]));  // open: clr
  Register Byte2 (.D(newContent[23:16]), .en(UpdateContentCtr), .clk(clock), .Q(contentOut[23:16]));  // open: clr
  Register Byte3 (.D(newContent[31:24]), .en(UpdateContentCtr), .clk(clock), .Q(contentOut[31:24]));  // open: clr
  Multiplexer #(.enable("false"), .width(2)) multiplexer_1 (
    .in0(NextAge), .in1(WayIndex), .out(multiplexer_1_out), .sel(InitializeCtr));
  Register #(.width(2)) register_1 (.D(multiplexer_1_out), .en(UpdateAgeCtr), .clk(clock), .Q(ageOut));  // open: clr
  Register #(.width(1)) register_2 (.D(IsValidValue), .en(IsValidValue), .clk(clock), .Q(isValid));  // open: clr
  not not_1 (not_1_out, IsValidValue);
  Register #(.width(1)) dirty (.D(not_1_out), .en(IsDirty_Ctr), .clk(clock), .Q(isDirty));  // open: clr
  Register #(.width(7)) tag (.D(Tagin), .en(UpdateContentCtr), .clk(clock), .Q(tagOut));  // open: clr

  // Other names for the same wires on the sheet: UpdateConentCtr = UpdateContentCtr
endmodule

module NextAge (
  input  [1:0] way0Age,
  input  [1:0] way1Age,
  input  [1:0] way2Age,
  input  [1:0] CurrentAge,
  output [1:0] way0NextAge,
  output [1:0] way1NextAge,
  output [1:0] way2NextAge
);

  wire comparator_1_eq, comparator_2_eq, comparator_3_eq, comparator_4_eq, comparator_5_eq, comparator_6_eq;
  wire [1:0] adder_1_out, adder_2_out, adder_3_out, multiplexer_1_out, multiplexer_2_out, multiplexer_3_out;

  Adder #(.width(2)) adder_1 (.a(way0Age), .b(2'b01), .out(adder_1_out));  // open: cin, cout
  Adder #(.width(2)) adder_2 (.a(way1Age), .b(2'b01), .out(adder_2_out));  // open: cin, cout
  Adder #(.width(2)) adder_3 (.a(way2Age), .b(2'b01), .out(adder_3_out));  // open: cin, cout
  Comparator #(.width(2)) comparator_1 (.a(CurrentAge), .b(way0Age), .eq(comparator_1_eq));  // open: gt, lt
  Comparator #(.width(2)) comparator_2 (.a(CurrentAge), .b(way1Age), .eq(comparator_2_eq));  // open: gt, lt
  Comparator #(.width(2)) comparator_3 (.a(CurrentAge), .b(way2Age), .eq(comparator_3_eq));  // open: gt, lt
  Comparator #(.width(2)) comparator_4 (.a(2'b10), .b(way0Age), .eq(comparator_4_eq));  // open: gt, lt
  Comparator #(.width(2)) comparator_5 (.a(2'b10), .b(way1Age), .eq(comparator_5_eq));  // open: gt, lt
  Multiplexer #(.enable("false"), .width(2)) multiplexer_1 (
    .in0(adder_2_out), .in1(way1Age), .out(multiplexer_1_out), .sel(comparator_5_eq));
  Comparator #(.width(2)) comparator_6 (.a(2'b10), .b(way2Age), .eq(comparator_6_eq));  // open: gt, lt
  Multiplexer #(.enable("false"), .width(2)) multiplexer_2 (
    .in0(adder_3_out), .in1(way2Age), .out(multiplexer_2_out), .sel(comparator_6_eq));
  Multiplexer #(.enable("false"), .width(2)) multiplexer_3 (
    .in0(adder_1_out), .in1(way0Age), .out(multiplexer_3_out), .sel(comparator_4_eq));
  Multiplexer #(.enable("false"), .width(2)) multiplexer_4 (
    .in0(multiplexer_3_out), .in1(2'b00), .out(way0NextAge), .sel(comparator_1_eq));
  Multiplexer #(.enable("false"), .width(2)) multiplexer_5 (
    .in0(multiplexer_1_out), .in1(2'b00), .out(way1NextAge), .sel(comparator_2_eq));
  Multiplexer #(.enable("false"), .width(2)) multiplexer_6 (
    .in0(multiplexer_2_out), .in1(2'b00), .out(way2NextAge), .sel(comparator_3_eq));
endmodule

module FindCurrentAge (
  input  [1:0] Way0Age,
  input  [1:0] Way1Age,
  input  [1:0] Way2Age,
  input  [6:0] Tag,
  input  [6:0] Way0Tag,
  input  [6:0] Way1Tag,
  input  [6:0] Way2Tag,
  output [1:0] CurrentAge
);

  wire and_1_out, and_2_out, and_3_out, and_4_out, and_5_out, and_6_out, and_7_out, and_8_out, and_9_out,
       and_10_out, and_11_out, and_12_out, and_13_out, and_14_out, and_15_out, comparator_1_eq,
       comparator_2_eq, comparator_3_eq, comparator_4_eq, comparator_5_eq, comparator_6_eq, comparator_7_eq,
       comparator_8_eq, comparator_9_eq, comparator_10_eq, comparator_11_eq, comparator_12_eq,
       comparator_13_eq, comparator_14_eq, comparator_15_eq, comparator_16_eq, comparator_17_eq,
       comparator_18_eq, comparator_19_eq, comparator_20_eq, comparator_21_eq, comparator_22_eq,
       comparator_23_eq, comparator_24_eq;
  wire [1:0] bitfinder_1_index, bitfinder_2_index, bitfinder_3_index, bitfinder_4_index, bitfinder_5_index,
       bitfinder_6_index, bitfinder_7_index, bitfinder_8_index, bitfinder_9_index, bitfinder_10_index,
       bitfinder_11_index, bitfinder_12_index, bitfinder_13_index, bitfinder_14_index, bitfinder_15_index,
       bitfinder_16_index, bitfinder_17_index, bitfinder_18_index, bitfinder_19_index, bitfinder_20_index,
       bitfinder_21_index, bitfinder_22_index, bitfinder_23_index, bitfinder_24_index, bitfinder_25_index,
       bitfinder_26_index, bitfinder_27_index, bitfinder_28_index, bitfinder_29_index, bitfinder_30_index,
       bitfinder_31_index, bitfinder_32_index, bitfinder_33_index, bitfinder_34_index, bitfinder_35_index,
       bitfinder_36_index, bitfinder_37_index, bitfinder_38_index, bitfinder_39_index, bitfinder_40_index,
       bitfinder_41_index, bitfinder_42_index, bitfinder_43_index, bitfinder_44_index, bitfinder_45_index,
       bitfinder_46_index, bitfinder_47_index, bitfinder_48_index;

  // Probe on Tag[3:0]
  // Probe on Way0Tag[3:0]
  // Probe on Way1Tag[3:0]
  // Probe on Way2Tag[3:0]
  BitFinder #(.width(4)) bitfinder_1 (.in(Tag[3:0]), .index(bitfinder_1_index));  // open: found
  BitFinder #(.width(4)) bitfinder_2 (.in(Way0Tag[3:0]), .index(bitfinder_2_index));  // open: found
  BitFinder #(.width(3)) bitfinder_3 (.in(Tag[6:4]), .index(bitfinder_3_index));  // open: found
  BitFinder #(.width(3)) bitfinder_4 (.in(Way0Tag[6:4]), .index(bitfinder_4_index));  // open: found
  BitFinder #(.\type ("high1"), .width(4)) bitfinder_5 (.in(Tag[3:0]), .index(bitfinder_5_index));  // open: found
  BitFinder #(.\type ("high1"), .width(3)) bitfinder_6 (.in(Tag[6:4]), .index(bitfinder_6_index));  // open: found
  BitFinder #(.\type ("high1"), .width(3)) bitfinder_7 (.in(Way0Tag[6:4]), .index(bitfinder_7_index));  // open: found
  // Probe on bitfinder_8_index
  BitFinder #(.\type ("low0"), .width(4)) bitfinder_8 (.in(Tag[3:0]), .index(bitfinder_8_index));  // open: found
  BitFinder #(.\type ("low0"), .width(4)) bitfinder_9 (.in(Way0Tag[3:0]), .index(bitfinder_9_index));  // open: found
  // Probe on bitfinder_10_index
  BitFinder #(.\type ("low0"), .width(3)) bitfinder_10 (.in(Tag[6:4]), .index(bitfinder_10_index));  // open: found
  // Probe on bitfinder_11_index
  BitFinder #(.\type ("low0"), .width(3)) bitfinder_11 (.in(Way0Tag[6:4]), .index(bitfinder_11_index));  // open: found
  // Probe on bitfinder_12_index
  BitFinder #(.\type ("high0"), .width(4)) bitfinder_12 (.in(Tag[3:0]), .index(bitfinder_12_index));  // open: found
  // Probe on bitfinder_13_index
  BitFinder #(.\type ("high0"), .width(4)) bitfinder_13 (.in(Way0Tag[3:0]), .index(bitfinder_13_index));  // open: found
  // Probe on bitfinder_14_index
  BitFinder #(.\type ("high0"), .width(3)) bitfinder_14 (.in(Tag[6:4]), .index(bitfinder_14_index));  // open: found
  // Probe on bitfinder_15_index
  BitFinder #(.\type ("high0"), .width(3)) bitfinder_15 (.in(Way0Tag[6:4]), .index(bitfinder_15_index));  // open: found
  // Probe on bitfinder_1_index
  // Probe on bitfinder_2_index
  // Probe on bitfinder_3_index
  // Probe on bitfinder_4_index
  // Probe on bitfinder_5_index
  // Probe on bitfinder_16_index
  BitFinder #(.\type ("high1"), .width(4)) bitfinder_16 (.in(Way0Tag[3:0]), .index(bitfinder_16_index));  // open: found
  // Probe on bitfinder_6_index
  // Probe on bitfinder_7_index
  // Probe on bitfinder_9_index
  Comparator #(.width(2)) comparator_1 (
    .a(bitfinder_14_index), .b(bitfinder_15_index), .eq(comparator_1_eq));  // open: gt, lt
  Comparator #(.width(2)) comparator_2 (
    .a(bitfinder_1_index), .b(bitfinder_2_index), .eq(comparator_2_eq));  // open: gt, lt
  Comparator #(.width(2)) comparator_3 (
    .a(bitfinder_3_index), .b(bitfinder_4_index), .eq(comparator_3_eq));  // open: gt, lt
  Comparator #(.width(2)) comparator_4 (
    .a(bitfinder_5_index), .b(bitfinder_16_index), .eq(comparator_4_eq));  // open: gt, lt
  Comparator #(.width(2)) comparator_5 (
    .a(bitfinder_6_index), .b(bitfinder_7_index), .eq(comparator_5_eq));  // open: gt, lt
  Comparator #(.width(2)) comparator_6 (
    .a(bitfinder_8_index), .b(bitfinder_9_index), .eq(comparator_6_eq));  // open: gt, lt
  Comparator #(.width(2)) comparator_7 (
    .a(bitfinder_10_index), .b(bitfinder_11_index), .eq(comparator_7_eq));  // open: gt, lt
  Comparator #(.width(2)) comparator_8 (
    .a(bitfinder_12_index), .b(bitfinder_13_index), .eq(comparator_8_eq));  // open: gt, lt
  and and_1 (and_1_out, comparator_2_eq, comparator_3_eq);
  and and_2 (and_2_out, comparator_4_eq, comparator_5_eq);
  and and_3 (and_3_out, comparator_6_eq, comparator_7_eq);
  and and_4 (and_4_out, comparator_8_eq, comparator_1_eq);
  and and_5 (and_5_out, and_1_out, and_2_out, and_3_out, and_4_out);
  // Probe on Way0Age
  // Probe on CurrentAge
  Multiplexer #(.enable("false"), .width(2)) multiplexer_1 (
    .in1(Way0Age), .out(CurrentAge), .sel(and_5_out));  // open: in0
  BitFinder #(.\type ("high0"), .width(3)) bitfinder_17 (.in(Tag[6:4]), .index(bitfinder_17_index));  // open: found
  BitFinder #(.width(4)) bitfinder_18 (.in(Tag[3:0]), .index(bitfinder_18_index));  // open: found
  BitFinder #(.width(4)) bitfinder_19 (.in(Way1Tag[3:0]), .index(bitfinder_19_index));  // open: found
  // Probe on bitfinder_20_index
  BitFinder #(.width(3)) bitfinder_20 (.in(Tag[6:4]), .index(bitfinder_20_index));  // open: found
  BitFinder #(.width(3)) bitfinder_21 (.in(Way1Tag[6:4]), .index(bitfinder_21_index));  // open: found
  BitFinder #(.\type ("high1"), .width(4)) bitfinder_22 (.in(Tag[3:0]), .index(bitfinder_22_index));  // open: found
  BitFinder #(.\type ("high1"), .width(4)) bitfinder_23 (.in(Way1Tag[3:0]), .index(bitfinder_23_index));  // open: found
  BitFinder #(.\type ("high1"), .width(3)) bitfinder_24 (.in(Tag[6:4]), .index(bitfinder_24_index));  // open: found
  BitFinder #(.\type ("high1"), .width(3)) bitfinder_25 (.in(Way1Tag[6:4]), .index(bitfinder_25_index));  // open: found
  // Probe on bitfinder_26_index
  BitFinder #(.\type ("low0"), .width(4)) bitfinder_26 (.in(Tag[3:0]), .index(bitfinder_26_index));  // open: found
  // Probe on bitfinder_27_index
  BitFinder #(.\type ("low0"), .width(4)) bitfinder_27 (.in(Way1Tag[3:0]), .index(bitfinder_27_index));  // open: found
  // Probe on bitfinder_28_index
  BitFinder #(.\type ("low0"), .width(3)) bitfinder_28 (.in(Tag[6:4]), .index(bitfinder_28_index));  // open: found
  // Probe on bitfinder_29_index
  BitFinder #(.\type ("low0"), .width(3)) bitfinder_29 (.in(Way1Tag[6:4]), .index(bitfinder_29_index));  // open: found
  // Probe on bitfinder_30_index
  BitFinder #(.\type ("high0"), .width(4)) bitfinder_30 (.in(Tag[3:0]), .index(bitfinder_30_index));  // open: found
  // Probe on bitfinder_31_index
  BitFinder #(.\type ("high0"), .width(4)) bitfinder_31 (.in(Way1Tag[3:0]), .index(bitfinder_31_index));  // open: found
  // Probe on bitfinder_17_index
  // Probe on bitfinder_32_index
  BitFinder #(.\type ("high0"), .width(3)) bitfinder_32 (.in(Way1Tag[6:4]), .index(bitfinder_32_index));  // open: found
  // Probe on bitfinder_18_index
  // Probe on bitfinder_19_index
  // Probe on bitfinder_21_index
  // Probe on bitfinder_22_index
  // Probe on bitfinder_23_index
  // Probe on bitfinder_24_index
  // Probe on bitfinder_25_index
  Comparator #(.width(2)) comparator_9 (
    .a(bitfinder_26_index), .b(bitfinder_27_index), .eq(comparator_9_eq));  // open: gt, lt
  Comparator #(.width(2)) comparator_10 (
    .a(bitfinder_28_index), .b(bitfinder_29_index), .eq(comparator_10_eq));  // open: gt, lt
  Comparator #(.width(2)) comparator_11 (
    .a(bitfinder_30_index), .b(bitfinder_31_index), .eq(comparator_11_eq));  // open: gt, lt
  Comparator #(.width(2)) comparator_12 (
    .a(bitfinder_17_index), .b(bitfinder_32_index), .eq(comparator_12_eq));  // open: gt, lt
  Comparator #(.width(2)) comparator_13 (
    .a(bitfinder_18_index), .b(bitfinder_19_index), .eq(comparator_13_eq));  // open: gt, lt
  Comparator #(.width(2)) comparator_14 (
    .a(bitfinder_20_index), .b(bitfinder_21_index), .eq(comparator_14_eq));  // open: gt, lt
  Comparator #(.width(2)) comparator_15 (
    .a(bitfinder_22_index), .b(bitfinder_23_index), .eq(comparator_15_eq));  // open: gt, lt
  Comparator #(.width(2)) comparator_16 (
    .a(bitfinder_24_index), .b(bitfinder_25_index), .eq(comparator_16_eq));  // open: gt, lt
  and and_6 (and_6_out, comparator_13_eq, comparator_14_eq);
  and and_7 (and_7_out, comparator_15_eq, comparator_16_eq);
  and and_8 (and_8_out, comparator_9_eq, comparator_10_eq);
  and and_9 (and_9_out, comparator_11_eq, comparator_12_eq);
  and and_10 (and_10_out, and_6_out, and_7_out, and_8_out, and_9_out);
  // Probe on Way1Age
  Multiplexer #(.enable("false"), .width(2)) multiplexer_2 (
    .in1(Way1Age), .out(CurrentAge), .sel(and_10_out));  // open: in0
  BitFinder #(.\type ("low0"), .width(4)) bitfinder_33 (.in(Tag[3:0]), .index(bitfinder_33_index));  // open: found
  BitFinder #(.\type ("low0"), .width(4)) bitfinder_34 (.in(Way2Tag[3:0]), .index(bitfinder_34_index));  // open: found
  BitFinder #(.\type ("low0"), .width(3)) bitfinder_35 (.in(Tag[6:4]), .index(bitfinder_35_index));  // open: found
  BitFinder #(.\type ("low0"), .width(3)) bitfinder_36 (.in(Way2Tag[6:4]), .index(bitfinder_36_index));  // open: found
  BitFinder #(.\type ("high0"), .width(4)) bitfinder_37 (.in(Tag[3:0]), .index(bitfinder_37_index));  // open: found
  BitFinder #(.\type ("high0"), .width(4)) bitfinder_38 (.in(Way2Tag[3:0]), .index(bitfinder_38_index));  // open: found
  BitFinder #(.\type ("high0"), .width(3)) bitfinder_39 (.in(Tag[6:4]), .index(bitfinder_39_index));  // open: found
  BitFinder #(.\type ("high0"), .width(3)) bitfinder_40 (.in(Way2Tag[6:4]), .index(bitfinder_40_index));  // open: found
  // Probe on bitfinder_41_index
  BitFinder #(.width(4)) bitfinder_41 (.in(Tag[3:0]), .index(bitfinder_41_index));  // open: found
  // Probe on bitfinder_42_index
  BitFinder #(.width(4)) bitfinder_42 (.in(Way2Tag[3:0]), .index(bitfinder_42_index));  // open: found
  // Probe on bitfinder_43_index
  BitFinder #(.width(3)) bitfinder_43 (.in(Tag[6:4]), .index(bitfinder_43_index));  // open: found
  // Probe on bitfinder_44_index
  BitFinder #(.width(3)) bitfinder_44 (.in(Way2Tag[6:4]), .index(bitfinder_44_index));  // open: found
  // Probe on bitfinder_45_index
  BitFinder #(.\type ("high1"), .width(4)) bitfinder_45 (.in(Tag[3:0]), .index(bitfinder_45_index));  // open: found
  // Probe on bitfinder_46_index
  BitFinder #(.\type ("high1"), .width(4)) bitfinder_46 (.in(Way2Tag[3:0]), .index(bitfinder_46_index));  // open: found
  // Probe on bitfinder_47_index
  BitFinder #(.\type ("high1"), .width(3)) bitfinder_47 (.in(Tag[6:4]), .index(bitfinder_47_index));  // open: found
  // Probe on bitfinder_48_index
  BitFinder #(.\type ("high1"), .width(3)) bitfinder_48 (.in(Way2Tag[6:4]), .index(bitfinder_48_index));  // open: found
  // Probe on bitfinder_33_index
  // Probe on bitfinder_34_index
  // Probe on bitfinder_35_index
  // Probe on bitfinder_36_index
  // Probe on bitfinder_37_index
  // Probe on bitfinder_38_index
  // Probe on bitfinder_39_index
  // Probe on bitfinder_40_index
  Comparator #(.width(2)) comparator_17 (
    .a(bitfinder_41_index), .b(bitfinder_42_index), .eq(comparator_17_eq));  // open: gt, lt
  Comparator #(.width(2)) comparator_18 (
    .a(bitfinder_43_index), .b(bitfinder_44_index), .eq(comparator_18_eq));  // open: gt, lt
  Comparator #(.width(2)) comparator_19 (
    .a(bitfinder_47_index), .b(bitfinder_48_index), .eq(comparator_19_eq));  // open: gt, lt
  Comparator #(.width(2)) comparator_20 (
    .a(bitfinder_33_index), .b(bitfinder_34_index), .eq(comparator_20_eq));  // open: gt, lt
  Comparator #(.width(2)) comparator_21 (
    .a(bitfinder_35_index), .b(bitfinder_36_index), .eq(comparator_21_eq));  // open: gt, lt
  Comparator #(.width(2)) comparator_22 (
    .a(bitfinder_37_index), .b(bitfinder_38_index), .eq(comparator_22_eq));  // open: gt, lt
  Comparator #(.width(2)) comparator_23 (
    .a(bitfinder_39_index), .b(bitfinder_40_index), .eq(comparator_23_eq));  // open: gt, lt
  Comparator #(.width(2)) comparator_24 (
    .a(bitfinder_45_index), .b(bitfinder_46_index), .eq(comparator_24_eq));  // open: gt, lt
  and and_11 (and_11_out, comparator_20_eq, comparator_21_eq);
  and and_12 (and_12_out, comparator_22_eq, comparator_23_eq);
  and and_13 (and_13_out, comparator_17_eq, comparator_18_eq);
  and and_14 (and_14_out, comparator_24_eq, comparator_19_eq);
  and and_15 (and_15_out, and_13_out, and_14_out, and_11_out, and_12_out);
  // Probe on Way2Age
  Multiplexer #(.enable("false"), .width(2)) multiplexer_3 (
    .in1(Way2Age), .out(CurrentAge), .sel(and_15_out));  // open: in0
  // Probe on CurrentAge

  // Other names for the same wires on the sheet: Tag1[3:0] = Tag[3:0]; Tag2[2:0] = Tag[6:4];
  //   Way0Tag1[3:0] = Way0Tag[3:0]; Way0Tag2[2:0] = Way0Tag[6:4]; Way1Tag1[3:0] = Way1Tag[3:0];
  //   Way1Tag2[2:0] = Way1Tag[6:4]; Way2Tag1[3:0] = Way2Tag[3:0]; Way2Tag2[2:0] = Way2Tag[6:4]
endmodule

module FindCurrentAgeSimple (
  input  [1:0] Way0Age,
  input  [1:0] Way1Age,
  input  [1:0] Way2Age,
  input  [1:0] matchingWay,
  output [1:0] CurrentAge
);

  Multiplexer #(.enable("false"), .select(2), .width(2)) multiplexer_1 (
    .in0(Way0Age), .in1(Way1Age), .in2(Way2Age), .out(CurrentAge), .sel(matchingWay));  // open: in3
endmodule

module WriteNewContent (
  input  [31:0] Way0Content,
  input  [31:0] Way1Content,
  input  [31:0] Way2Content,
  input  [1:0] Offset,
  input  [7:0] WriteValue,
  input  [1:0] Matchingway,
  output [31:0] out_7
);

  wire comparator_1_eq, comparator_2_eq, comparator_3_eq, comparator_4_eq, comparator_5_eq, comparator_6_eq,
       comparator_7_eq, comparator_8_eq, comparator_9_eq, comparator_10_eq, comparator_11_eq,
       comparator_12_eq;
  wire [7:0] multiplexer_1_out, multiplexer_2_out, multiplexer_3_out, multiplexer_4_out, multiplexer_5_out,
       multiplexer_6_out, multiplexer_7_out, multiplexer_8_out, multiplexer_9_out, multiplexer_10_out,
       multiplexer_11_out, multiplexer_12_out;

  Comparator #(.width(2)) comparator_1 (.a(Offset), .b(2'b00), .eq(comparator_1_eq));  // open: gt, lt
  Multiplexer #(.enable("false"), .width(8)) multiplexer_1 (
    .in0(Way0Content[7:0]), .in1(WriteValue), .out(multiplexer_1_out), .sel(comparator_1_eq));
  Comparator #(.width(2)) comparator_2 (.a(Offset), .b(2'b01), .eq(comparator_2_eq));  // open: gt, lt
  Comparator #(.width(2)) comparator_3 (.a(Offset), .b(2'b10), .eq(comparator_3_eq));  // open: gt, lt
  Comparator #(.width(2)) comparator_4 (.a(Offset), .b(2'b11), .eq(comparator_4_eq));  // open: gt, lt
  Comparator #(.width(2)) comparator_5 (.a(Offset), .b(2'b00), .eq(comparator_5_eq));  // open: gt, lt
  Multiplexer #(.enable("false"), .width(8)) multiplexer_2 (
    .in0(Way1Content[7:0]), .in1(WriteValue), .out(multiplexer_2_out), .sel(comparator_5_eq));
  Comparator #(.width(2)) comparator_6 (.a(Offset), .b(2'b01), .eq(comparator_6_eq));  // open: gt, lt
  Comparator #(.width(2)) comparator_7 (.a(Offset), .b(2'b10), .eq(comparator_7_eq));  // open: gt, lt
  Comparator #(.width(2)) comparator_8 (.a(Offset), .b(2'b11), .eq(comparator_8_eq));  // open: gt, lt
  Comparator #(.width(2)) comparator_9 (.a(Offset), .b(2'b00), .eq(comparator_9_eq));  // open: gt, lt
  Comparator #(.width(2)) comparator_10 (.a(Offset), .b(2'b01), .eq(comparator_10_eq));  // open: gt, lt
  Comparator #(.width(2)) comparator_11 (.a(Offset), .b(2'b10), .eq(comparator_11_eq));  // open: gt, lt
  Multiplexer #(.enable("false"), .width(8)) multiplexer_3 (
    .in0(Way0Content[15:8]), .in1(WriteValue), .out(multiplexer_3_out), .sel(comparator_2_eq));
  Multiplexer #(.enable("false"), .width(8)) multiplexer_4 (
    .in0(Way0Content[23:16]), .in1(WriteValue), .out(multiplexer_4_out), .sel(comparator_3_eq));
  Multiplexer #(.enable("false"), .width(8)) multiplexer_5 (
    .in0(Way0Content[31:24]), .in1(WriteValue), .out(multiplexer_5_out), .sel(comparator_4_eq));
  Multiplexer #(.enable("false"), .width(8)) multiplexer_6 (
    .in0(Way1Content[15:8]), .in1(WriteValue), .out(multiplexer_6_out), .sel(comparator_6_eq));
  Multiplexer #(.enable("false"), .width(8)) multiplexer_7 (
    .in0(Way1Content[23:16]), .in1(WriteValue), .out(multiplexer_7_out), .sel(comparator_7_eq));
  Multiplexer #(.enable("false"), .width(8)) multiplexer_8 (
    .in0(Way1Content[31:24]), .in1(WriteValue), .out(multiplexer_8_out), .sel(comparator_8_eq));
  Multiplexer #(.enable("false"), .width(8)) multiplexer_9 (
    .in0(Way2Content[7:0]), .in1(WriteValue), .out(multiplexer_9_out), .sel(comparator_9_eq));
  Multiplexer #(.enable("false"), .width(8)) multiplexer_10 (
    .in0(Way2Content[15:8]), .in1(WriteValue), .out(multiplexer_10_out), .sel(comparator_10_eq));
  Multiplexer #(.enable("false"), .width(8)) multiplexer_11 (
    .in0(Way2Content[23:16]), .in1(WriteValue), .out(multiplexer_11_out), .sel(comparator_11_eq));
  Comparator #(.width(2)) comparator_12 (.a(Offset), .b(2'b11), .eq(comparator_12_eq));  // open: gt, lt
  Multiplexer #(.enable("false"), .width(8)) multiplexer_12 (
    .in0(Way2Content[31:24]), .in1(WriteValue), .out(multiplexer_12_out), .sel(comparator_12_eq));
  Multiplexer #(.enable("false"), .select(2), .width(32)) multiplexer_13 (
    .in0({multiplexer_5_out, multiplexer_4_out, multiplexer_3_out, multiplexer_1_out}),
    .in1({multiplexer_8_out, multiplexer_7_out, multiplexer_6_out, multiplexer_2_out}),
    .in2({multiplexer_12_out, multiplexer_11_out, multiplexer_10_out, multiplexer_9_out}), .out(out_7),
    .sel(Matchingway));  // open: in3

  // Other names for the same wires on the sheet: NewContent[31:0] = out_7
endmodule

module FsmNextState (
  input  didContain_In,
  input  IsDirty_In,
  input  CpuRead_In,
  input  CpuWrite_In,
  input  [2:0] CurrentState,
  output [2:0] NextState
);

  wire and_1_out, and_2_out, and_3_out, and_4_out, and_5_out, and_6_out, and_7_out, and_8_out, and_9_out,
       and_10_out, and_11_out, and_12_out, not_1_out, not_2_out, not_3_out, not_4_out, not_5_out, not_6_out;

  not not_1 (not_1_out, didContain_In);
  not not_2 (not_2_out, IsDirty_In);
  not not_3 (not_3_out, CpuRead_In);
  not not_4 (not_4_out, CurrentState[2]);
  not not_5 (not_5_out, CurrentState[1]);
  not not_6 (not_6_out, CurrentState[0]);
  and and_1 (and_1_out, CurrentState[1], CurrentState[0]);
  and and_2 (and_2_out, not_3_out, CurrentState[2], not_6_out);
  and and_3 (and_3_out, CurrentState[2], CurrentState[1]);
  and and_4 (and_4_out, didContain_In, CurrentState[1]);
  and and_5 (and_5_out, not_4_out, CurrentState[0]);
  and and_6 (and_6_out, not_1_out, CurrentState[1], not_6_out);
  and and_7 (and_7_out, CurrentState[2], CurrentState[1], not_6_out);
  and and_8 (and_8_out, not_1_out, not_6_out);
  and and_9 (and_9_out, not_5_out, not_6_out);
  and and_10 (and_10_out, not_2_out, not_4_out, CurrentState[1], CurrentState[0]);
  and and_11 (and_11_out, CurrentState[2], not_5_out);
  and and_12 (and_12_out, CurrentState[2], not_6_out);
  or or_1 (NextState[2], and_1_out, and_2_out, and_3_out, and_4_out);
  or or_2 (NextState[1], and_5_out, and_6_out, and_7_out);
  or or_3 (NextState[0], and_8_out, and_9_out, and_10_out, and_11_out, and_12_out);
endmodule

module OutputCircuit (
  input  [2:0] CurrentState,
  output Ready_Ctr,
  output MemRead_Ctr,
  output MemWrite_Ctr,
  output Initialize_Ctr,
  output UpdateAge_Ctr,
  output IsValid_Value,
  output IsDirty_Ctr,
  output UpdateContent_Ctr
);

  wire not_1_out, not_2_out, not_3_out;

  not not_1 (not_1_out, CurrentState[2]);
  not not_2 (not_2_out, CurrentState[1]);
  not not_3 (not_3_out, CurrentState[0]);
  and and_1 (Ready_Ctr, not_1_out, not_2_out, CurrentState[0]);
  and and_2 (MemRead_Ctr, CurrentState[2], CurrentState[1], CurrentState[0]);
  and and_3 (MemWrite_Ctr, CurrentState[2], CurrentState[1], not_3_out);
  and and_4 (Initialize_Ctr, not_1_out, not_2_out, not_3_out);
  and and_5 (UpdateAge_Ctr, CurrentState[2], not_2_out, not_3_out);
  and and_6 (IsValid_Value, CurrentState[2], CurrentState[1], CurrentState[0]);
  and and_7 (IsDirty_Ctr, CurrentState[2], CurrentState[0]);
  and and_8 (UpdateContent_Ctr, CurrentState[2], CurrentState[0]);
endmodule
